# Fritzing sketch proyecto_final_ejemplo_sensor (saved by Fritzing 0.9.1b)
breadboards: 1

parts:
  Parte1 = Arduino Uno (Rev3)
  RHT1 = Humidity and Temperature Sensor RHT03

nets:
  N1: Parte1.D7, RHT1.Data-signal
  5V: Parte1.5V, RHT1.Vcc
  N2: Parte1.GND, RHT1.GND_2
